# Fritzing sketch 02-LED, Arduino, Breadboard (saved by Fritzing 0.9.3b)
breadboards: 1

parts:
  LED1 = LED - 5mm [color="Red (633nm)" package="5 mm [THT]"]
  R1 = Resistor [tolerance=±5% resistance=220 package=THT]
  Arduino_UNO_R3 = Arduino Uno (Rev3)

nets:
  N1: LED1.cathode, Arduino_UNO_R3.GND
  N2: LED1.anode, R1.Pin_0
  N3: R1.Pin_1, Arduino_UNO_R3.5V
